// Logisim project DustcatV.circ as structural Verilog
module CPU (
);

  wire clock_1_out;
  wire [3:0] decodeissue_1_decode_dest, decodeissue_1_decode_qj, decodeissue_1_decode_qk;
  wire [7:0] decodeissue_1_decode_op;
  wire [31:0] instructionfetch_1_inst_out;

  Clock clock_1 (.out(clock_1_out));
  InstructionFetch instructionfetch_1 (.CLK_IN(clock_1_out), .INST_OUT(instructionfetch_1_inst_out));
  DecodeIssue decodeissue_1 (
    .CLK_IN(clock_1_out), .INST_IN(instructionfetch_1_inst_out), .DECODE_OP(decodeissue_1_decode_op),
    .DECODE_DEST(decodeissue_1_decode_dest), .DECODE_QJ(decodeissue_1_decode_qj),
    .DECODE_QK(decodeissue_1_decode_qk));  // open: DECODE_CONST
  Execute execute_1 (
    .Ex_OPIN(decodeissue_1_decode_op), .EX_DESTIN(decodeissue_1_decode_dest),
    .EX_QJIN(decodeissue_1_decode_qj), .EX_QKIN(decodeissue_1_decode_qk), .CLK_IN(clock_1_out));  // open: CBDOUT1, CDBOUT2, CDBOUT3LSU
endmodule

module DecodeIssue (
  input  CLK_IN,
  input  [31:0] INST_IN,
  output [7:0] DECODE_OP,
  output [3:0] DECODE_DEST,
  output [3:0] DECODE_QJ,
  output [3:0] DECODE_QK,
  output [15:0] DECODE_CONST
);
endmodule

module Execute (
  input  [7:0] Ex_OPIN,
  input  [3:0] EX_DESTIN,
  input  [3:0] EX_QJIN,
  input  [3:0] EX_QKIN,
  input  CLK_IN,
  output [36:0] CBDOUT1,
  output [36:0] CDBOUT2,
  output [36:0] CDBOUT3LSU
);

  wire integerfunctionalunit_1_funit_running, integerfunctionalunit_2_funit_running,
       loadstoreunit_1_funit_running, reservationstation_1_loadunit, reservationstation_2_loadunit,
       reservationstation_3_loadunit;
  wire [3:0] reservationstation_1_dest, reservationstation_2_dest, reservationstation_3_dest;
  wire [7:0] reservationstation_1_op, reservationstation_2_op, reservationstation_3_op;
  wire [31:0] reservationstation_1_aout, reservationstation_1_bout, reservationstation_2_aout,
       reservationstation_2_bout, reservationstation_3_aout, reservationstation_3_bout;

  ReservationStation reservationstation_1 (
    .CLKIN(CLK_IN), .IsUnitRunning(loadstoreunit_1_funit_running), .CBDIN1(CBDOUT1), .CBDIN2(CDBOUT2),
    .CBDIN3(CDBOUT3LSU), .LoadUnit(reservationstation_1_loadunit), .OP(reservationstation_1_op),
    .DEST(reservationstation_1_dest), .AOUT(reservationstation_1_aout), .BOUT(reservationstation_1_bout));  // open: OPIN, DESTIN, QJIN, QKIN
  ReservationStation reservationstation_2 (
    .CLKIN(CLK_IN), .IsUnitRunning(integerfunctionalunit_1_funit_running), .CBDIN1(CBDOUT1),
    .CBDIN2(CDBOUT2), .CBDIN3(CDBOUT3LSU), .LoadUnit(reservationstation_2_loadunit),
    .OP(reservationstation_2_op), .DEST(reservationstation_2_dest), .AOUT(reservationstation_2_aout),
    .BOUT(reservationstation_2_bout));  // open: OPIN, DESTIN, QJIN, QKIN
  ReservationStation reservationstation_3 (
    .CLKIN(CLK_IN), .IsUnitRunning(integerfunctionalunit_2_funit_running), .CBDIN1(CBDOUT1),
    .CBDIN2(CDBOUT2), .CBDIN3(CDBOUT3LSU), .LoadUnit(reservationstation_3_loadunit),
    .OP(reservationstation_3_op), .DEST(reservationstation_3_dest), .AOUT(reservationstation_3_aout),
    .BOUT(reservationstation_3_bout));  // open: OPIN, DESTIN, QJIN, QKIN
  LoadStoreUnit loadstoreunit_1 (
    .OP_IN(reservationstation_1_op), .ADDRESS_IN(reservationstation_1_aout),
    .DATA_IN(reservationstation_1_bout), .DEST_IN(reservationstation_1_dest),
    .LOAD_UNIT(reservationstation_1_loadunit), .CLK_IN(CLK_IN),
    .FUNIT_RUNNING(loadstoreunit_1_funit_running), .CDB_OUT(CDBOUT3LSU));
  IntegerFunctionalUnit integerfunctionalunit_1 (
    .OP_IN(reservationstation_2_op), .A_IN(reservationstation_2_aout), .B_IN(reservationstation_2_bout),
    .DEST_IN(reservationstation_2_dest), .LOAD_UNIT(reservationstation_2_loadunit), .CLK_IN(CLK_IN),
    .FUNIT_RUNNING(integerfunctionalunit_1_funit_running), .CDB_OUT(CBDOUT1));
  IntegerFunctionalUnit integerfunctionalunit_2 (
    .OP_IN(reservationstation_3_op), .A_IN(reservationstation_3_aout), .B_IN(reservationstation_3_bout),
    .DEST_IN(reservationstation_3_dest), .LOAD_UNIT(reservationstation_3_loadunit), .CLK_IN(CLK_IN),
    .FUNIT_RUNNING(integerfunctionalunit_2_funit_running), .CDB_OUT(CDBOUT2));
  Pull_Resistor pull_resistor_1 (.node(CBDOUT1));
  Pull_Resistor pull_resistor_2 (.node(CDBOUT2));
  Pull_Resistor pull_resistor_3 (.node(CDBOUT3LSU));
endmodule

module InstructionFetch (
  input  CLK_IN,
  output [31:0] INST_OUT
);

  Pull_Resistor pull_resistor_1 (.node(INST_OUT));

  // Notes on the sheet:
  //   INST_OUT: pull=down
endmodule

module ArchitecturalRegisterFile (
  input  [31:0] ARF_Data,
  input  [3:0] ARF_A_Sel,
  input  [3:0] ARF_B_Sel,
  input  [3:0] ARF_Write_Sel,
  input  ARF_Write,
  input  ARF_Clk,
  output [31:0] ARF_A,
  output [31:0] ARF_B
);

  wire demultiplexer_1_out1, demultiplexer_1_out2, demultiplexer_1_out3, demultiplexer_1_out4,
       demultiplexer_1_out5, demultiplexer_1_out6, demultiplexer_1_out7, demultiplexer_1_out8,
       demultiplexer_1_out9, demultiplexer_1_out10, demultiplexer_1_out11, demultiplexer_1_out12,
       demultiplexer_1_out13, demultiplexer_1_out14, demultiplexer_1_out15;
  wire [31:0] register_1_q, register_2_q, register_3_q, register_4_q, register_5_q, register_6_q,
       register_7_q, register_8_q, register_9_q, register_10_q, register_11_q, register_12_q, register_13_q,
       register_14_q, register_15_q;

  Demultiplexer #(.select(4)) demultiplexer_1 (
    .out1(demultiplexer_1_out1), .out2(demultiplexer_1_out2), .out3(demultiplexer_1_out3),
    .out4(demultiplexer_1_out4), .out5(demultiplexer_1_out5), .out6(demultiplexer_1_out6),
    .out7(demultiplexer_1_out7), .out8(demultiplexer_1_out8), .out9(demultiplexer_1_out9),
    .out10(demultiplexer_1_out10), .out11(demultiplexer_1_out11), .out12(demultiplexer_1_out12),
    .out13(demultiplexer_1_out13), .out14(demultiplexer_1_out14), .out15(demultiplexer_1_out15),
    .in(ARF_Write), .sel(ARF_Write_Sel));  // open: out0
  Register #(.width(32)) register_1 (
    .D(ARF_Data), .en(demultiplexer_1_out1), .clk(ARF_Clk), .Q(register_1_q));  // open: clr
  Register #(.width(32)) register_2 (
    .D(ARF_Data), .en(demultiplexer_1_out2), .clk(ARF_Clk), .Q(register_2_q));  // open: clr
  Register #(.width(32)) register_3 (
    .D(ARF_Data), .en(demultiplexer_1_out3), .clk(ARF_Clk), .Q(register_3_q));  // open: clr
  Register #(.width(32)) register_4 (
    .D(ARF_Data), .en(demultiplexer_1_out4), .clk(ARF_Clk), .Q(register_4_q));  // open: clr
  Register #(.width(32)) register_5 (
    .D(ARF_Data), .en(demultiplexer_1_out5), .clk(ARF_Clk), .Q(register_5_q));  // open: clr
  Register #(.width(32)) register_6 (
    .D(ARF_Data), .en(demultiplexer_1_out6), .clk(ARF_Clk), .Q(register_6_q));  // open: clr
  Register #(.width(32)) register_7 (
    .D(ARF_Data), .en(demultiplexer_1_out7), .clk(ARF_Clk), .Q(register_7_q));  // open: clr
  Register #(.width(32)) register_8 (
    .D(ARF_Data), .en(demultiplexer_1_out8), .clk(ARF_Clk), .Q(register_8_q));  // open: clr
  Register #(.width(32)) register_9 (
    .D(ARF_Data), .en(demultiplexer_1_out9), .clk(ARF_Clk), .Q(register_9_q));  // open: clr
  Register #(.width(32)) register_10 (
    .D(ARF_Data), .en(demultiplexer_1_out10), .clk(ARF_Clk), .Q(register_10_q));  // open: clr
  Register #(.width(32)) register_11 (
    .D(ARF_Data), .en(demultiplexer_1_out11), .clk(ARF_Clk), .Q(register_11_q));  // open: clr
  Register #(.width(32)) register_12 (
    .D(ARF_Data), .en(demultiplexer_1_out12), .clk(ARF_Clk), .Q(register_12_q));  // open: clr
  Register #(.width(32)) register_13 (
    .D(ARF_Data), .en(demultiplexer_1_out13), .clk(ARF_Clk), .Q(register_13_q));  // open: clr
  Register #(.width(32)) register_14 (
    .D(ARF_Data), .en(demultiplexer_1_out14), .clk(ARF_Clk), .Q(register_14_q));  // open: clr
  Register #(.width(32)) register_15 (
    .D(ARF_Data), .en(demultiplexer_1_out15), .clk(ARF_Clk), .Q(register_15_q));  // open: clr
  Multiplexer #(.select(4), .width(32)) multiplexer_1 (
    .in0({32{1'b0}}), .in1(register_1_q), .in2(register_2_q), .in3(register_3_q), .in4(register_4_q),
    .in5(register_5_q), .in6(register_6_q), .in7(register_7_q), .in8(register_8_q), .in9(register_9_q),
    .in10(register_10_q), .in11(register_11_q), .in12(register_12_q), .in13(register_13_q),
    .in14(register_14_q), .in15(register_15_q), .out(ARF_A), .sel(ARF_A_Sel));
  Multiplexer #(.select(4), .width(32)) multiplexer_2 (
    .in0({32{1'b0}}), .in1(register_1_q), .in2(register_2_q), .in3(register_3_q), .in4(register_4_q),
    .in5(register_5_q), .in6(register_6_q), .in7(register_7_q), .in8(register_8_q), .in9(register_9_q),
    .in10(register_10_q), .in11(register_11_q), .in12(register_12_q), .in13(register_13_q),
    .in14(register_14_q), .in15(register_15_q), .out(ARF_B), .sel(ARF_B_Sel));

  // Notes on the sheet:
  //   ARF_A: pull=down
  //   ARF_B: pull=down
endmodule

module ReservationStation (
  input  [7:0] OPIN,
  input  [3:0] DESTIN,
  input  [3:0] QJIN,
  input  [3:0] QKIN,
  input  CLKIN,
  input  IsUnitRunning,
  input  [36:0] CBDIN1,
  input  [36:0] CBDIN2,
  input  [36:0] CBDIN3,
  output LoadUnit,
  output [7:0] OP,
  output [3:0] DEST,
  output [31:0] AOUT,
  output [31:0] BOUT
);

  wire and_2_out, buffer_1_out, buffer_2_out, buffer_3_out, buffer_4_out, buffer_5_out, demultiplexer_1_out0,
       demultiplexer_1_out1, demultiplexer_1_out2, demultiplexer_1_out3, demultiplexer_2_out0,
       demultiplexer_2_out1, demultiplexer_2_out2, demultiplexer_2_out3, not_1_out, not_2_out,
       priority_encoder_1_gs, priority_encoder_2_gs, register_3_q, reservationstationline_1_isfree,
       reservationstationline_1_ready, reservationstationline_2_isfree, reservationstationline_2_ready,
       reservationstationline_3_isfree, reservationstationline_3_ready, reservationstationline_4_isfree,
       reservationstationline_4_ready;
  wire [2:0] priority_encoder_1_out, pull_resistor_9_node, register_1_q, register_2_q;
  wire [3:0] reservationstationline_1_dest_out, reservationstationline_2_dest_out,
       reservationstationline_3_dest_out, reservationstationline_4_dest_out;
  wire [7:0] reservationstationline_1_op_out, reservationstationline_2_op_out,
       reservationstationline_3_op_out, reservationstationline_4_op_out;
  wire [31:0] reservationstationline_1_a_out, reservationstationline_1_b_out, reservationstationline_2_a_out,
       reservationstationline_2_b_out, reservationstationline_3_a_out, reservationstationline_3_b_out,
       reservationstationline_4_a_out, reservationstationline_4_b_out;

  Demultiplexer #(.select(3)) demultiplexer_1 (
    .out0(demultiplexer_1_out0), .out1(demultiplexer_1_out1), .out2(demultiplexer_1_out2),
    .out3(demultiplexer_1_out3), .in(register_3_q), .sel(register_2_q));  // open: out4, out5, out6, out7
  Pull_Resistor pull_resistor_1 (.node(CLKIN));
  Pull_Resistor pull_resistor_2 (.node(CBDIN1));
  Pull_Resistor pull_resistor_3 (.node(CBDIN2));
  Demultiplexer #(.select(3)) demultiplexer_2 (
    .out0(demultiplexer_2_out0), .out1(demultiplexer_2_out1), .out2(demultiplexer_2_out2),
    .out3(demultiplexer_2_out3), .in(buffer_1_out), .sel(register_1_q));  // open: out4, out5, out6, out7
  buf buffer_1 (buffer_1_out, buffer_2_out);
  Pull_Resistor pull_resistor_4 (.node(CBDIN3));
  buf buffer_2 (buffer_2_out, buffer_3_out);
  buf buffer_3 (buffer_3_out, buffer_4_out);
  buf buffer_4 (buffer_4_out, buffer_5_out);
  buf buffer_5 (buffer_5_out, LoadUnit);
  ReservationStationLine reservationstationline_1 (
    .CBDIN1(CBDIN1), .CBDIN2(CBDIN2), .CBDIN3(CBDIN3), .OP_IN(OPIN), .Dest_IN(DESTIN), .QJ_IN(QJIN),
    .QK_IN(QKIN), .CLEAR(demultiplexer_2_out0), .CLK_IN(CLKIN), .Write(demultiplexer_1_out0),
    .Ready(reservationstationline_1_ready), .IsFree(reservationstationline_1_isfree),
    .Op_out(reservationstationline_1_op_out), .Dest_out(reservationstationline_1_dest_out),
    .A_out(reservationstationline_1_a_out), .B_out(reservationstationline_1_b_out));
  ReservationStationLine reservationstationline_2 (
    .CBDIN1(CBDIN1), .CBDIN2(CBDIN2), .CBDIN3(CBDIN3), .OP_IN(OPIN), .Dest_IN(DESTIN), .QJ_IN(QJIN),
    .QK_IN(QKIN), .CLEAR(demultiplexer_2_out1), .CLK_IN(CLKIN), .Write(demultiplexer_1_out1),
    .Ready(reservationstationline_2_ready), .IsFree(reservationstationline_2_isfree),
    .Op_out(reservationstationline_2_op_out), .Dest_out(reservationstationline_2_dest_out),
    .A_out(reservationstationline_2_a_out), .B_out(reservationstationline_2_b_out));
  ReservationStationLine reservationstationline_3 (
    .CBDIN1(CBDIN1), .CBDIN2(CBDIN2), .CBDIN3(CBDIN3), .OP_IN(OPIN), .Dest_IN(DESTIN), .QJ_IN(QJIN),
    .QK_IN(QKIN), .CLEAR(demultiplexer_2_out2), .CLK_IN(CLKIN), .Write(demultiplexer_1_out2),
    .Ready(reservationstationline_3_ready), .IsFree(reservationstationline_3_isfree),
    .Op_out(reservationstationline_3_op_out), .Dest_out(reservationstationline_3_dest_out),
    .A_out(reservationstationline_3_a_out), .B_out(reservationstationline_3_b_out));
  ReservationStationLine reservationstationline_4 (
    .CBDIN1(CBDIN1), .CBDIN2(CBDIN2), .CBDIN3(CBDIN3), .OP_IN(OPIN), .Dest_IN(DESTIN), .QJ_IN(QJIN),
    .QK_IN(QKIN), .CLEAR(demultiplexer_2_out3), .CLK_IN(CLKIN), .Write(demultiplexer_1_out3),
    .Ready(reservationstationline_4_ready), .IsFree(reservationstationline_4_isfree),
    .Op_out(reservationstationline_4_op_out), .Dest_out(reservationstationline_4_dest_out),
    .A_out(reservationstationline_4_a_out), .B_out(reservationstationline_4_b_out));
  Pull_Resistor pull_resistor_5 (.node(IsUnitRunning));
  not not_1 (not_1_out, IsUnitRunning);
  Priority_Encoder priority_encoder_1 (
    .in0(reservationstationline_1_ready), .in1(reservationstationline_2_ready),
    .in2(reservationstationline_3_ready), .in3(reservationstationline_4_ready), .out(priority_encoder_1_out),
    .en_in(CLKIN), .gs(priority_encoder_1_gs));  // open: in4, in5, in6, in7, en_out
  Pull_Resistor pull_resistor_6 (.node(OP));
  Multiplexer #(.select(3), .width(8)) multiplexer_1 (
    .in0(reservationstationline_1_op_out), .in1(reservationstationline_2_op_out),
    .in2(reservationstationline_3_op_out), .in3(reservationstationline_4_op_out), .out(OP), .sel(register_1_q));  // open: in4, in5, in6, in7
  Multiplexer #(.select(3), .width(4)) multiplexer_2 (
    .in0(reservationstationline_1_dest_out), .in1(reservationstationline_2_dest_out),
    .in2(reservationstationline_3_dest_out), .in3(reservationstationline_4_dest_out), .out(DEST),
    .sel(register_1_q));  // open: in4, in5, in6, in7
  Multiplexer #(.select(3), .width(32)) multiplexer_3 (
    .in0(reservationstationline_1_a_out), .in1(reservationstationline_2_a_out),
    .in2(reservationstationline_3_a_out), .in3(reservationstationline_4_a_out), .out(AOUT), .sel(register_1_q));  // open: in4, in5, in6, in7
  Multiplexer #(.select(3), .width(32)) multiplexer_4 (
    .in0(reservationstationline_1_b_out), .in1(reservationstationline_2_b_out),
    .in2(reservationstationline_3_b_out), .in3(reservationstationline_4_b_out), .out(BOUT), .sel(register_1_q));  // open: in4, in5, in6, in7
  Register #(.width(3)) register_1 (
    .D(priority_encoder_1_out), .en(CLKIN), .clk(CLKIN), .Q(register_1_q));  // open: clr
  Pull_Resistor pull_resistor_7 (.node(priority_encoder_1_out));
  and and_1 (LoadUnit, priority_encoder_1_gs, not_1_out, CLKIN);
  Pull_Resistor pull_resistor_8 (.node(register_1_q));
  Pull_Resistor pull_resistor_9 (.node(pull_resistor_9_node));
  Priority_Encoder priority_encoder_2 (
    .in0(reservationstationline_1_isfree), .in1(reservationstationline_2_isfree),
    .in2(reservationstationline_3_isfree), .in3(reservationstationline_4_isfree), .out(pull_resistor_9_node),
    .gs(priority_encoder_2_gs));  // open: in4, in5, in6, in7, en_in, en_out
  and and_2 (and_2_out, priority_encoder_2_gs, CLKIN);
  Pull_Resistor pull_resistor_10 (.node(LoadUnit));
  Pull_Resistor pull_resistor_11 (.node(OP));
  Pull_Resistor pull_resistor_12 (.node(DEST));
  Pull_Resistor pull_resistor_13 (.node(AOUT));
  Pull_Resistor pull_resistor_14 (.node(BOUT));
  Register #(.width(3)) register_2 (.D(pull_resistor_9_node), .en(CLKIN), .clk(CLKIN), .Q(register_2_q));  // open: clr
  Register #(.trigger("high"), .width(1)) register_3 (
    .D(and_2_out), .en(CLKIN), .clk(CLKIN), .Q(register_3_q), .clr(not_2_out));
  not not_2 (not_2_out, CLKIN);
  Pull_Resistor pull_resistor_15 (.node(register_2_q));
endmodule

module ReservationStationLine (
  input  [36:0] CBDIN1,
  input  [36:0] CBDIN2,
  input  [36:0] CBDIN3,
  input  [7:0] OP_IN,
  input  [3:0] Dest_IN,
  input  [3:0] QJ_IN,
  input  [3:0] QK_IN,
  input  CLEAR,
  input  CLK_IN,
  input  Write,
  output Ready,
  output IsFree,
  output [7:0] Op_out,
  output [3:0] Dest_out,
  output [31:0] A_out,
  output [31:0] B_out
);

  wire buffer_1_out, buffer_2_out, buffer_3_out, comparator_1_eq, comparator_2_eq, comparator_3_eq,
       comparator_5_eq, comparator_6_eq, comparator_7_eq, comparator_8_eq, comparator_9_eq, not_1_out,
       not_2_out, or_1_out, priority_encoder_1_p4, priority_encoder_2_p4;
  wire [1:0] priority_encoder_1_p2, priority_encoder_2_p2;
  wire [3:0] QJ_q, QK_q;
  wire [31:0] multiplexer_1_out, multiplexer_2_out;

  buf buffer_1 (buffer_1_out, CLK_IN);
  buf buffer_2 (buffer_2_out, buffer_1_out);
  buf buffer_3 (buffer_3_out, buffer_2_out);
  Comparator #(.width(4)) comparator_1 (.a(CBDIN1[36:33]), .b(QJ_q), .eq(comparator_1_eq));  // open: gt, lt
  Comparator #(.width(4)) comparator_2 (.a(CBDIN2[36:33]), .b(QJ_q), .eq(comparator_2_eq));  // open: gt, lt
  Comparator #(.width(4)) comparator_3 (.a(CBDIN3[36:33]), .b(QJ_q), .eq(comparator_3_eq));  // open: gt, lt
  Register register_1 (.D(OP_IN), .en(Write), .clk(Write), .Q(Op_out), .clr(CLEAR));
  Pull_Resistor pull_resistor_1 (.node(comparator_1_eq));
  Pull_Resistor pull_resistor_2 (.node(comparator_2_eq));
  Pull_Resistor pull_resistor_3 (.node(comparator_3_eq));
  Register #(.width(4)) Dest (.D(Dest_IN), .en(Write), .clk(Write), .Q(Dest_out), .clr(CLEAR));
  Comparator comparator_4 (.a(Op_out), .b({8{1'b0}}), .eq(IsFree));  // open: gt, lt
  // Priority_Encoder #(.select(2)) priority_encoder_1: pin names not known; wires that end beside it: comparator_3_eq, priority_encoder_1_p2, comparator_2_eq, priority_encoder_1_p4, comparator_1_eq
  Multiplexer #(.select(2), .width(32)) multiplexer_1 (
    .in1(CBDIN3[31:0]), .in2(CBDIN2[31:0]), .in3(CBDIN1[31:0]), .out(multiplexer_1_out),
    .sel(priority_encoder_1_p2));  // open: in0
  Register #(.width(4)) QJ (.D(QJ_IN), .en(Write), .clk(Write), .Q(QJ_q), .clr(CLEAR));
  Register #(.width(4)) QK (.D(QK_IN), .en(Write), .clk(Write), .Q(QK_q), .clr(CLEAR));
  Comparator #(.width(4)) comparator_5 (.a(CBDIN1[36:33]), .b(QK_q), .eq(comparator_5_eq));  // open: gt, lt
  Comparator #(.width(4)) comparator_6 (.a(CBDIN2[36:33]), .b(QK_q), .eq(comparator_6_eq));  // open: gt, lt
  Comparator #(.width(4)) comparator_7 (.a(CBDIN3[36:33]), .b(QK_q), .eq(comparator_7_eq));  // open: gt, lt
  or or_1 (or_1_out, CLEAR, Write);
  // Priority_Encoder #(.select(2)) priority_encoder_2: pin names not known; wires that end beside it: comparator_7_eq, priority_encoder_2_p2, comparator_6_eq, priority_encoder_2_p4, comparator_5_eq
  Multiplexer #(.select(2), .width(32)) multiplexer_2 (
    .in1(CBDIN3[31:0]), .in2(CBDIN2[31:0]), .in3(CBDIN1[31:0]), .out(multiplexer_2_out),
    .sel(priority_encoder_2_p2));  // open: in0
  Register #(.width(32)) VJ (
    .D(multiplexer_1_out), .en(priority_encoder_1_p4), .clk(buffer_3_out), .Q(A_out), .clr(or_1_out));
  Register #(.width(32)) VK (
    .D(multiplexer_2_out), .en(priority_encoder_2_p4), .clk(buffer_3_out), .Q(B_out), .clr(or_1_out));
  Comparator #(.width(32)) comparator_8 (.a(B_out), .b({32{1'b0}}), .eq(comparator_8_eq));  // open: gt, lt
  not not_1 (not_1_out, comparator_8_eq);
  not not_2 (not_2_out, comparator_9_eq);
  Comparator #(.width(32)) comparator_9 (.a(A_out), .b({32{1'b0}}), .eq(comparator_9_eq));  // open: gt, lt
  and and_1 (Ready, not_1_out, not_2_out);
endmodule

module IntegerFunctionalUnit (
  input  [7:0] OP_IN,
  input  [31:0] A_IN,
  input  [31:0] B_IN,
  input  [3:0] DEST_IN,
  input  LOAD_UNIT,
  input  CLK_IN,
  output FUNIT_RUNNING,
  output [36:0] CDB_OUT
);

  Pull_Resistor pull_resistor_1 (.node(FUNIT_RUNNING));
  Pull_Resistor pull_resistor_2 (.node(CDB_OUT));

  // Notes on the sheet:
  //   CLK_IN: pull=down
endmodule

module LoadStoreUnit (
  input  [7:0] OP_IN,
  input  [31:0] ADDRESS_IN,
  input  [31:0] DATA_IN,
  input  [3:0] DEST_IN,
  input  LOAD_UNIT,
  input  CLK_IN,
  output FUNIT_RUNNING,
  output [36:0] CDB_OUT
);

  Pull_Resistor pull_resistor_1 (.node(FUNIT_RUNNING));
  Pull_Resistor pull_resistor_2 (.node(CDB_OUT));

  // Notes on the sheet:
  //   CLK_IN: pull=down
endmodule
